# Fritzing sketch wiring (saved by Fritzing 0.9.3b)

parts:
  U1 = TB6621FNG [package=ssop24]
  U2 = lolin
  Right_Motor = DC Motor
  Left_Motor = DC Motor
  BAT1 = Battery Holders [package=lipo-1100mAh]
  BAT2 = Battery Holders [package=lipo-1100mAh]

nets:
  N1: U1.A01, Right_Motor.pin_2
  N2: U1.A02, Right_Motor.pin_1
  N3: U1.B02, Left_Motor.pin_2
  N4: U1.B01, Left_Motor.pin_1
  N5: U1.PWMB, U2.connector4
  N6: U1.BIN2, U2.connector9
  N7: U1.BIN1, U2.connector8
  N8: U1.GND, U2.connector15, BAT2.-
  N9: U1.VCC, U2.connector14
  N10: U1.AIN1, U2.connector10
  N11: U1.AIN2, U2.connector11
  N12: U1.PWMA, U2.connector5
  N13: U1.VM1, BAT2.+
  N14: U2.connector16, BAT1.+
  N15: U2.connector17, BAT1.-
